// Logisim project processor.circ as structural Verilog: 19 circuits, main circuit processor
module processor (
  input  in_1,
  input  in_2,
  input  in_3,
  input  in_4,
  input  in_5,
  output [15:0] R0,
  output [15:0] R2,
  output [15:0] R1,
  output [15:0] R3
);

  wire alu_1_carry, alu_1_neg, alu_1_zero, branch_1_jmp, clock_1_out, control_1_absjmp, control_1_alutobus,
       control_1_brk, control_1_immstore, control_1_ioread, control_1_iowrite, control_1_ld,
       control_1_select_a, control_1_st_pc, control_1_str, control_1_we, gpo_1_out_5, gpo_1_out_6,
       gpo_1_out_7, gpo_1_out_8, gpo_1_out_9, gpo_1_out_10, gpo_1_out_11, gpo_1_out_12, gpo_1_out_13,
       gpo_1_out_14, gpo_1_out_15, gpo_1_out_16, gpo_1_out_17, gpo_1_out_18, gpo_1_out_19, gpo_1_out_20,
       keyboard_2_enable, terminal_1_termenable;
  wire [2:0] control_1_branch, control_1_select_b;
  wire [4:0] control_1_alu_ctrl;
  wire [6:0] keyboard_1_data, terminal_1_ascii;
  wire [15:0] alu_1_y, controlled_buffer_1_out, graphic_1_out_5, graphic_1_out_6, graphic_1_out_7,
       graphic_1_out_8, graphic_1_out_9, graphic_1_out_10, graphic_1_out_11, graphic_1_out_12,
       graphic_1_out_13, graphic_1_out_14, graphic_1_out_15, graphic_1_out_16, graphic_1_out_17,
       graphic_1_out_18, graphic_1_out_19, graphic_1_out_20, imReg_immediate, multiplexer_1_out,
       multiplexer_2_out, pc_1_act_pc, pc_1_next_seq_pc, registers_1_dest_2, registers_1_source_2,
       rom_1_data, SignExtend__5_bit_dest, SignExtend__5_bit_source, SignExtend__9_bit;

  Clock clock_1 (.out(clock_1_out));
  TTY #(.rows(10)) tty_1 (.data(terminal_1_ascii), .clk(clock_1_out), .we(terminal_1_termenable));  // open: clr
  PC pc_1 (
    .ALU_out(alu_1_y), .act_PC(pc_1_act_pc), .next_seq_PC(pc_1_next_seq_pc), .Clock(clock_1_out),
    .rel__jmp(branch_1_jmp), .abs__jmp(control_1_absjmp), .BRK(control_1_brk));
  ROM #(.addrWidth(16), .dataWidth(16)) rom_1 (.addr(pc_1_act_pc), .data(rom_1_data));  // open: sel
  assign controlled_buffer_1_out = control_1_st_pc ? pc_1_next_seq_pc : 16'bz;  // Controlled_Buffer controlled_buffer_1
  imReg imReg (.instruction(rom_1_data), .immediate(imReg_immediate), .En(control_1_immstore), .Takt(clock_1_out));
  control control_1 (
    .Opcode(rom_1_data[15:9]), .WE(control_1_we), .ALUToBus(control_1_alutobus),
    .Select_B(control_1_select_b), .ALU_ctrl(control_1_alu_ctrl), .branch(control_1_branch),
    .str(control_1_str), .ld(control_1_ld), .ST_PC(control_1_st_pc), .Select_A(control_1_select_a),
    .ImmStore(control_1_immstore), .AbsJmp(control_1_absjmp), .ioWrite(control_1_iowrite),
    .ioRead(control_1_ioread), .BRK(control_1_brk), .BRKEn(in_1));
  terminal terminal_1 (
    .data(registers_1_source_2), .addr(alu_1_y), .ASCII(terminal_1_ascii),
    .TermEnable(terminal_1_termenable), .io_Write(control_1_iowrite));
  registers registers_1 (
    .Write(controlled_buffer_1_out), .dest_2(registers_1_dest_2), .source_2(registers_1_source_2),
    .WE(control_1_we), .dest(rom_1_data[7:4]), .Clock(clock_1_out), .R0(R0), .R1(R1),
    .source(rom_1_data[3:0]), .R2(R2), .R3(R3));
  SignExtend SignExtend (
    .Instruction(rom_1_data), ._9_Bit(SignExtend__9_bit), ._5_Bit_Dest(SignExtend__5_bit_dest),
    ._5_Bit_Source(SignExtend__5_bit_source));
  Multiplexer #(.select(3), .width(16), .enable("false")) multiplexer_1 (
    .in0(registers_1_source_2), .in1(imReg_immediate), .in2({16{1'b0}}), .in3(16'hff), .in4(16'hfff),
    .in5(SignExtend__5_bit_source), .in6(SignExtend__9_bit), .in7(SignExtend__5_bit_dest),
    .out(multiplexer_1_out), .sel(control_1_select_b));
  Keyboard keyboard_1 (.clk(clock_1_out), .re(keyboard_2_enable), .data(keyboard_1_data));  // open: clr, avail
  Multiplexer #(.width(16), .enable("false")) multiplexer_2 (
    .in0(registers_1_dest_2), .in1(registers_1_source_2), .out(multiplexer_2_out), .sel(control_1_select_a));
  assign controlled_buffer_1_out = control_1_alutobus ? alu_1_y : 16'bz;  // Controlled_Buffer controlled_buffer_2
  ALU alu_1 (
    .A(multiplexer_2_out), .B(multiplexer_1_out), .Y(alu_1_y), .Zero(alu_1_zero), .Carry(alu_1_carry),
    .Clock(clock_1_out), .Operation(control_1_alu_ctrl), .Neg(alu_1_neg));
  branch branch_1 (.Ctrl(control_1_branch), .Jmp(branch_1_jmp), .C(alu_1_carry), .Z(alu_1_zero), .N(alu_1_neg));
  keyboard keyboard_2 (
    .data(controlled_buffer_1_out), .addr(alu_1_y), .io_Read(control_1_ioread), .ASCII(keyboard_1_data),
    .Enable(keyboard_2_enable));
  RAM #(.addrWidth(16), .dataWidth(16), .bus("separate")) ram_1 (
    .addr(alu_1_y), .din(registers_1_source_2), .data(controlled_buffer_1_out), .str(control_1_str),
    .clk(clock_1_out), .ld(control_1_ld));  // open: sel, clr
  DotMatrix #(.matrixcols(16), .matrixrows(16)) dotmatrix_1 (
    .col0(graphic_1_out_5), .col1(graphic_1_out_6), .col2(graphic_1_out_7), .col3(graphic_1_out_8),
    .col4(graphic_1_out_9), .col5(graphic_1_out_10), .col6(graphic_1_out_11), .col7(graphic_1_out_12),
    .col8(graphic_1_out_13), .col9(graphic_1_out_14), .col10(graphic_1_out_15), .col11(graphic_1_out_16),
    .col12(graphic_1_out_17), .col13(graphic_1_out_18), .col14(graphic_1_out_19), .col15(graphic_1_out_20));
  graphic graphic_1 (
    .Data(registers_1_source_2), .Takt(clock_1_out), .Enable(control_1_iowrite), .Addr(alu_1_y),
    .out_5(graphic_1_out_5), .out_6(graphic_1_out_6), .out_7(graphic_1_out_7), .out_8(graphic_1_out_8),
    .out_9(graphic_1_out_9), .out_10(graphic_1_out_10), .out_11(graphic_1_out_11), .out_12(graphic_1_out_12),
    .out_13(graphic_1_out_13), .out_14(graphic_1_out_14), .out_15(graphic_1_out_15),
    .out_16(graphic_1_out_16), .out_17(graphic_1_out_17), .out_18(graphic_1_out_18),
    .out_19(graphic_1_out_19), .out_20(graphic_1_out_20));
  GPO gpo_1 (
    .data(registers_1_source_2), .clock(clock_1_out), .addr(alu_1_y), .io_Write(control_1_iowrite),
    .out_5(gpo_1_out_5), .out_6(gpo_1_out_6), .out_7(gpo_1_out_7), .out_8(gpo_1_out_8), .out_9(gpo_1_out_9),
    .out_10(gpo_1_out_10), .out_11(gpo_1_out_11), .out_12(gpo_1_out_12), .out_13(gpo_1_out_13),
    .out_14(gpo_1_out_14), .out_15(gpo_1_out_15), .out_16(gpo_1_out_16), .out_17(gpo_1_out_17),
    .out_18(gpo_1_out_18), .out_19(gpo_1_out_19), .out_20(gpo_1_out_20));
  GPI gpi_1 (
    .data(controlled_buffer_1_out), .addr(alu_1_y), .io_Read(control_1_ioread), .in_1(in_2), .in_2(in_3),
    .in_3(in_4), .in_4(in_5));  // open: in_5, in_6, in_7, in_8, in_9, in_10, in_11, in_12, in_13, in_15, in_16, in_17
  LED led_1 (.in(gpo_1_out_5));
  LED led_2 (.in(gpo_1_out_6));
  LED led_3 (.in(gpo_1_out_7));
  LED led_4 (.in(gpo_1_out_8));
  LED led_5 (.in(gpo_1_out_9));
  LED led_6 (.in(gpo_1_out_10));
  LED led_7 (.in(gpo_1_out_11));
  LED led_8 (.in(gpo_1_out_12));
  LED led_9 (.in(gpo_1_out_13));
  LED led_10 (.in(gpo_1_out_14));
  LED led_11 (.in(gpo_1_out_15));
  LED led_12 (.in(gpo_1_out_16));
  LED led_13 (.in(gpo_1_out_17));
  LED led_14 (.in(gpo_1_out_18));
  LED led_15 (.in(gpo_1_out_19));
  LED led_16 (.in(gpo_1_out_20));

  // Notes on the sheet:
  //   Programm
  //   contents of rom_1 (hex, n*v repeats v):
  //   1400 5260 5320 8022 5000 8020 1200 5250 52a0 53c0 8021 5000 8021 1200 5310 803a 1200 8020 5000 8046
  //   1200 5380 8061 1200 5270 52c0 53a0 8064 1200 5300 8065 1200 5200 52f0 5350 53e0 8067 1200 53b0 806c
  //   1200 5280 5290 5390 806f 1200 5230 8070 1200 52b0 8072 1200 5210 5220 5240 5360 5370 8073 1200 52d0
  //   52e0 53d0 8074 1200 53f0 1470 1000 1405 3c05 5e01 6edd 3c04 6401 6eda 3c04 6401 6ed7 1401 2001 5e01
  //   6ed3 1471 1407 1415 401 3c0c 5e01 6ecc 150e 151e 401 803c 3a00 5e01 6ec5 1472 1407 1415 801 3c02
  //   5e01 6ebe 8023 1200 8021 1210 801 3c02 5e01 6eb6 1473 1407 1415 1421 4020 601 3c0d 5e01 6ead 1474
  //   1407 1415 1421 4020 a01 3c01 5e01 6ea4 1475 ffff 1300 4600 ffff 3b00 5e01 6e9c ffff 1200 4600 bfff
  //   3a00 5e01 6e95 1401 4600 5c01 6e91 4600 6201 6e8e 1476 9234 1200 4800 b412 3a00 5e01 6e86 9234 1200
  //   4a00 a143 3a00 5e01 6e7f 1477 3c80 5e01 6e7b 1481 80ac 6800 80ac 1210 1480 3810 5e01 6e72 1478 3c80
  //   5e01 6e6e 80bb 1200 1482 6a00 6e69 1480 1479 1407 3603 3d05 5e01 6e62 1407 8028 3400 8118 3a00 5e01
  //   6e5b 1407 1413 3201 3d05 5e01 6e55 147a 1405 5330 1801 5340 5713 3c15 5e01 6e4c 5714 3c16 5e01 6e48
  //   1533 4e43 3c45 5e01 6e43 1831 4e43 3c46 5e01 6e3e 147b 1533 1405 4c30 1801 1831 4c30 5723 3c25 5e01
  //   6e33 5724 3c26 5e01 6e2f 147c 140f 5330 140f 8004 5a10 3c1f 5e01 6e26 147d 1500 1510 8004 5810 5714
  //   3d10 5e01 6e1d 147e 3c80 5e01 6e19 1484 fffe 1200 7c00 1801 6601 6e12 1801 6001 6e0f 1480 3c80 5e08
  //   1505 812c 68f0 208 8132 68f0 7c00 6fff 1407 812c 68f0 6fff 1400 812c 68f0 207 8132 68f0 7c00 6fff
  //   4e10 73f1 1801 3c10 65fb 6a0f 4800 4a00 8141 6820 4a00 8141 6820 4800 4a00 8141 6820 4a00 8141 6820
  //   6a0f 210 281f 3c1a 6203 8030 1610 6e02 8037 1610 73f1 6a02
  //   RAM
endmodule

// Registers
module registers (
  input  [15:0] Write,
  input  [3:0] source,
  input  WE,
  input  [3:0] dest,
  input  Clock,
  output [15:0] R0,
  output [15:0] R1,
  output [15:0] R2,
  output [15:0] R3,
  output [15:0] dest_2,
  output [15:0] source_2
);

  wire demultiplexer_1_out0, demultiplexer_1_out1, demultiplexer_1_out2, demultiplexer_1_out3,
       demultiplexer_1_out4, demultiplexer_1_out5, demultiplexer_1_out6, demultiplexer_1_out7,
       demultiplexer_1_out8, demultiplexer_1_out9, demultiplexer_1_out10, demultiplexer_1_out11,
       demultiplexer_1_out12, demultiplexer_1_out13, demultiplexer_1_out14, demultiplexer_1_out15;
  wire [15:0] R4_q, R5_q, R6_q, R7_q, R8_q, R9_q, R10_q, R11_q, R12_q, R13_q, RA_q, SP_q;

  Demultiplexer #(.select(4), .enable("false")) demultiplexer_1 (
    .out0(demultiplexer_1_out0), .out1(demultiplexer_1_out1), .out2(demultiplexer_1_out2),
    .out3(demultiplexer_1_out3), .out4(demultiplexer_1_out4), .out5(demultiplexer_1_out5),
    .out6(demultiplexer_1_out6), .out7(demultiplexer_1_out7), .out8(demultiplexer_1_out8),
    .out9(demultiplexer_1_out9), .out10(demultiplexer_1_out10), .out11(demultiplexer_1_out11),
    .out12(demultiplexer_1_out12), .out13(demultiplexer_1_out13), .out14(demultiplexer_1_out14),
    .out15(demultiplexer_1_out15), .in(WE), .sel(dest));
  Register #(.width(16)) u_R0 (.D(Write), .en(demultiplexer_1_out0), .Q(R0), .clk(Clock));  // open: clr
  Register #(.width(16)) u_R1 (.D(Write), .en(demultiplexer_1_out1), .Q(R1), .clk(Clock));  // open: clr
  Register #(.width(16)) u_R2 (.D(Write), .en(demultiplexer_1_out2), .Q(R2), .clk(Clock));  // open: clr
  Register #(.width(16)) u_R3 (.D(Write), .en(demultiplexer_1_out3), .Q(R3), .clk(Clock));  // open: clr
  Register #(.width(16)) R4 (.D(Write), .en(demultiplexer_1_out4), .Q(R4_q), .clk(Clock));  // open: clr
  Register #(.width(16)) R5 (.D(Write), .en(demultiplexer_1_out5), .Q(R5_q), .clk(Clock));  // open: clr
  Register #(.width(16)) R6 (.D(Write), .en(demultiplexer_1_out6), .Q(R6_q), .clk(Clock));  // open: clr
  Register #(.width(16)) R7 (.D(Write), .en(demultiplexer_1_out7), .Q(R7_q), .clk(Clock));  // open: clr
  Register #(.width(16)) R8 (.D(Write), .en(demultiplexer_1_out8), .Q(R8_q), .clk(Clock));  // open: clr
  Register #(.width(16)) R9 (.D(Write), .en(demultiplexer_1_out9), .Q(R9_q), .clk(Clock));  // open: clr
  Register #(.width(16)) R10 (.D(Write), .en(demultiplexer_1_out10), .Q(R10_q), .clk(Clock));  // open: clr
  Register #(.width(16)) R11 (.D(Write), .en(demultiplexer_1_out11), .Q(R11_q), .clk(Clock));  // open: clr
  Register #(.width(16)) R12 (.D(Write), .en(demultiplexer_1_out12), .Q(R12_q), .clk(Clock));  // open: clr
  Register #(.width(16)) R13 (.D(Write), .en(demultiplexer_1_out13), .Q(R13_q), .clk(Clock));  // open: clr
  Register #(.width(16)) RA (.D(Write), .en(demultiplexer_1_out14), .Q(RA_q), .clk(Clock));  // open: clr
  Register #(.width(16)) SP (.D(Write), .en(demultiplexer_1_out15), .Q(SP_q), .clk(Clock));  // open: clr
  Multiplexer #(.select(4), .width(16), .enable("false")) multiplexer_1 (
    .in0(R0), .in1(R1), .in2(R2), .in3(R3), .in4(R4_q), .in5(R5_q), .in6(R6_q), .in7(R7_q), .in8(R8_q),
    .in9(R9_q), .in10(R10_q), .in11(R11_q), .in12(R12_q), .in13(R13_q), .in14(RA_q), .in15(SP_q),
    .out(dest_2), .sel(dest));
  Multiplexer #(.select(4), .width(16), .enable("false")) multiplexer_2 (
    .in0(R0), .in1(R1), .in2(R2), .in3(R3), .in4(R4_q), .in5(R5_q), .in6(R6_q), .in7(R7_q), .in8(R8_q),
    .in9(R9_q), .in10(R10_q), .in11(R11_q), .in12(R12_q), .in13(R13_q), .in14(RA_q), .in15(SP_q),
    .out(source_2), .sel(source));
endmodule

module ALU (
  input  [15:0] A,
  input  [15:0] B,
  input  Clock,
  input  [4:0] Operation,
  output [15:0] Y,
  output Zero,
  output Neg,
  output Carry
);

  wire adder_1_cout, and_2_out, asr_1_lsb_out, comparator_1_eq, comparator_1_lt, lsl_1_msb_out,
       lsr_1_lsb_out, multiplexer_1_out, multiplexer_2_out, subtractor_1_bout;
  wire [15:0] adder_1_out, and_1_out, asr_1_out, lsl_1_out, lsr_1_out, multiplier_1_out, or_1_out,
       subtractor_1_out, swap_1_out, swapn_1_out, xor_1_out;

  Adder #(.width(16)) adder_1 (.a(A), .b(B), .out(adder_1_out), .cin(and_2_out), .cout(adder_1_cout));
  Subtractor #(.width(16)) subtractor_1 (
    .a(A), .b(B), .out(subtractor_1_out), .bin(and_2_out), .bout(subtractor_1_bout));
  assign and_1_out = A & B;  // AND_Gate and_1, 16 bits wide
  assign or_1_out = A | B;  // OR_Gate or_1, 16 bits wide
  assign xor_1_out = A ^ B;  // XOR_Gate xor_1, 16 bits wide
  LSL lsl_1 (.LSB_In(and_2_out), .Data(A), .Out(lsl_1_out), .MSB_Out(lsl_1_msb_out));
  LSR lsr_1 (.Data(A), .MSB_In(and_2_out), .LSB_Out(lsr_1_lsb_out), .Out(lsr_1_out));
  ASR asr_1 (.Data(A), .LSB_Out(asr_1_lsb_out), .Out(asr_1_out));
  swap swap_1 (.Data(A), .Out(swap_1_out));
  swapN swapn_1 (.Data(A), .Out(swapn_1_out));
  Multiplier #(.width(16)) multiplier_1 (.a(A), .b(B), .out(multiplier_1_out));  // open: cin, cout
  and and_2 (and_2_out, Operation[4], Carry);
  Multiplexer #(.select(4), .enable("false")) multiplexer_1 (
    .in0(Carry), .in1(adder_1_cout), .in2(subtractor_1_bout), .in3(Carry), .in4(Carry), .in5(Carry),
    .in6(lsl_1_msb_out), .in7(lsr_1_lsb_out), .in8(asr_1_lsb_out), .in9(Carry), .in10(Carry), .in11(Carry),
    .in12(Carry), .in13(Carry), .in14(Carry), .in15(Carry), .out(multiplexer_1_out), .sel(Operation[3:0]));
  Multiplexer #(.select(4), .enable("false")) multiplexer_2 (
    .in0(1'b0), .in1(1'b1), .in2(1'b1), .in3(1'b0), .in4(1'b0), .in5(1'b0), .in6(1'b1), .in7(1'b1),
    .in8(1'b1), .in9(1'b0), .in10(1'b0), .in11(1'b0), .in12(1'b0), .in13(1'b0), .in14(1'b0), .in15(1'b0),
    .out(multiplexer_2_out), .sel(Operation[3:0]));
  D_Flip_Flop u_Carry (
    .clk(Clock), .D(multiplexer_1_out), .Q(Carry), .en(multiplexer_2_out));  // open: Qn, preset, reset
  Multiplexer #(.select(4), .width(16), .enable("false")) multiplexer_3 (
    .in0(B), .in1(adder_1_out), .in2(subtractor_1_out), .in3(and_1_out), .in4(or_1_out), .in5(xor_1_out),
    .in6(lsl_1_out), .in7(lsr_1_out), .in8(asr_1_out), .in9(swap_1_out), .in10(swapn_1_out),
    .in11(multiplier_1_out), .out(Y), .sel(Operation[3:0]));  // open: in12, in13, in14, in15
  Comparator #(.width(16)) comparator_1 (
    .a(Y), .b({16{1'b0}}), .eq(comparator_1_eq), .lt(comparator_1_lt));  // open: gt
  D_Flip_Flop u_Zero (.clk(Clock), .D(comparator_1_eq), .Q(Zero), .en(multiplexer_2_out));  // open: Qn, preset, reset
  D_Flip_Flop u_Neg (.clk(Clock), .D(comparator_1_lt), .Q(Neg), .en(multiplexer_2_out));  // open: Qn, preset, reset
endmodule

module LSL (
  input  LSB_In,
  input  [15:0] Data,
  output [15:0] Out,
  output MSB_Out
);


  assign MSB_Out = Data[15];
  assign Out = {Data[14:0], LSB_In};
endmodule

module LSR (
  input  [15:0] Data,
  input  MSB_In,
  output LSB_Out,
  output [15:0] Out
);


  assign LSB_Out = Data[0];
  assign Out = {MSB_In, Data[15:1]};
endmodule

module ASR (
  input  [15:0] Data,
  output LSB_Out,
  output [15:0] Out
);


  assign LSB_Out = Data[0];
  assign Out = {{2{Data[15]}}, Data[14:1]};
endmodule

module swap (
  input  [15:0] Data,
  output [15:0] Out
);


  assign Out = {Data[7:0], Data[15:8]};
endmodule

module swapN (
  input  [15:0] Data,
  output [15:0] Out
);


  assign Out = {Data[11:8], Data[15:12], Data[3:0], Data[7:4]};
endmodule

module branch (
  input  C,
  input  Z,
  input  N,
  input  [2:0] Ctrl,
  output Jmp
);

  wire multiplexer_1_out;

  Multiplexer #(.select(2), .enable("false")) multiplexer_1 (
    .in0(1'b0), .in1(C), .in2(Z), .in3(N), .out(multiplexer_1_out), .sel(Ctrl[1:0]));
  xor xor_1 (Jmp, multiplexer_1_out, Ctrl[2]);
endmodule

module control (
  input  [6:0] Opcode,
  input  BRKEn,
  output ImmStore,
  output AbsJmp,
  output Select_A,
  output ALUToBus,
  output [2:0] Select_B,
  output [4:0] ALU_ctrl,
  output WE,
  output [2:0] branch,
  output ST_PC,
  output str,
  output ld,
  output ioWrite,
  output ioRead,
  output BRK
);

  wire not_1_out;
  wire [5:0] multiplexer_1_out;
  wire [23:20] rom_1_data;

  Multiplexer #(.width(6), .enable("false")) multiplexer_1 (
    .in0(Opcode[5:0]), .in1({6{1'b0}}), .out(multiplexer_1_out), .sel(Opcode[6]));
  not not_1 (not_1_out, BRKEn);
  and and_1 (BRK, rom_1_data[20], not_1_out);
  ROM #(.addrWidth(6), .dataWidth(24)) rom_1 (
    .addr(multiplexer_1_out),
    .data({rom_1_data, ioRead, ioWrite, branch, ALU_ctrl, Select_A, ST_PC, WE, ALUToBus, AbsJmp, Select_B, str, ld}));  // open: sel

  assign ImmStore = Opcode[6];

  // Notes on the sheet:
  //   BRKEn: pull=down
  //   contents of rom_1 (hex, n*v repeats v):
  //   0 c0 4c0 44c0 8c0 48c0 cc0 10c0 14c0 c4 d4 4c4 4d4 44c4 44d4 8c4 8d4 48c4 48d4 cc4 cd4 10c4 10d4
  //   14c4 14d4 2cc0 2cc4 2cd4 800 804 814 18c0 1cc0 58c0 5cc0 20c0 24c0 28c0 40a 689 6 1e 85 95 406 685
  //   8018 10018 18018 28018 30018 38018 1a4 20 24 20018 40004 4001c 40408 80284 80294 80688 100000
endmodule

module PC (
  input  [15:0] ALU_out,
  input  BRK,
  input  Clock,
  input  rel__jmp,
  input  abs__jmp,
  output [15:0] next_seq_PC,
  output [15:0] act_PC
);

  wire not_1_out;
  wire [15:0] adder_2_out, multiplexer_1_out, multiplexer_2_out;

  not not_1 (not_1_out, BRK);
  Register #(.width(16), .trigger("falling")) PC (
    .D(multiplexer_2_out), .en(not_1_out), .Q(act_PC), .clk(Clock));  // open: clr
  Adder #(.width(16)) adder_1 (.a(act_PC), .b(16'h1), .out(next_seq_PC));  // open: cin, cout
  Adder #(.width(16)) adder_2 (.a(next_seq_PC), .b(ALU_out), .out(adder_2_out));  // open: cin, cout
  Multiplexer #(.width(16), .enable("false")) multiplexer_1 (
    .in0(next_seq_PC), .in1(adder_2_out), .out(multiplexer_1_out), .sel(rel__jmp));
  Multiplexer #(.width(16), .enable("false")) multiplexer_2 (
    .in0(multiplexer_1_out), .in1(ALU_out), .out(multiplexer_2_out), .sel(abs__jmp));

  // Notes on the sheet:
  //   rel__jmp: pull=down
  //   abs__jmp: pull=down
endmodule

module imReg (
  input  [15:0] instruction,
  input  En,
  input  Takt,
  output [15:0] immediate
);

  wire [15:15] register_1_q;

  Register #(.width(16)) register_1 (
    .D(instruction), .en(En), .Q({register_1_q[15], immediate[14:0]}), .clk(Takt));  // open: clr

  assign immediate[15] = instruction[8];
endmodule

module SignExtend (
  input  [15:0] Instruction,
  output [15:0] _9_Bit,
  output [15:0] _5_Bit_Dest,
  output [15:0] _5_Bit_Source
);


  assign _5_Bit_Dest = {{11{1'b0}}, Instruction[8:4]};
  assign _5_Bit_Source = {{11{1'b0}}, Instruction[8], Instruction[3:0]};
  assign _9_Bit = {{8{Instruction[8]}}, Instruction[7:0]};
endmodule

module brk (
  input  Taster,
  input  BRK,
  output clkout
);

  wire and_1_out, clock_1_out, not_1_out;

  Clock clock_1 (.out(clock_1_out));
  not not_1 (not_1_out, BRK);
  and and_1 (and_1_out, clock_1_out, not_1_out);
  or or_1 (clkout, Taster, and_1_out);
endmodule

module graphic (
  input  [15:0] Data,
  input  Takt,
  input  Enable,
  input  [15:0] Addr,
  output [15:0] out_5,
  output [15:0] out_6,
  output [15:0] out_7,
  output [15:0] out_8,
  output [15:0] out_9,
  output [15:0] out_10,
  output [15:0] out_11,
  output [15:0] out_12,
  output [15:0] out_13,
  output [15:0] out_14,
  output [15:0] out_15,
  output [15:0] out_16,
  output [15:0] out_17,
  output [15:0] out_18,
  output [15:0] out_19,
  output [15:0] out_20
);

  wire demultiplexer_1_out0, demultiplexer_1_out1, demultiplexer_1_out2, demultiplexer_1_out3,
       demultiplexer_1_out4, demultiplexer_1_out5, demultiplexer_1_out6, demultiplexer_1_out7,
       demultiplexer_1_out8, demultiplexer_1_out9, demultiplexer_1_out10, demultiplexer_1_out11,
       demultiplexer_1_out12, demultiplexer_1_out13, demultiplexer_1_out14, demultiplexer_1_out15,
       demultiplexer_1_out16;
  wire [15:0] register_1_q, register_2_q, register_3_q, register_4_q, register_5_q, register_6_q,
       register_7_q, register_8_q, register_9_q, register_10_q, register_11_q, register_12_q, register_13_q,
       register_14_q, register_15_q, register_16_q;

  Demultiplexer #(.select(5), .enable("false")) demultiplexer_1 (
    .out0(demultiplexer_1_out0), .out1(demultiplexer_1_out1), .out2(demultiplexer_1_out2),
    .out3(demultiplexer_1_out3), .out4(demultiplexer_1_out4), .out5(demultiplexer_1_out5),
    .out6(demultiplexer_1_out6), .out7(demultiplexer_1_out7), .out8(demultiplexer_1_out8),
    .out9(demultiplexer_1_out9), .out10(demultiplexer_1_out10), .out11(demultiplexer_1_out11),
    .out12(demultiplexer_1_out12), .out13(demultiplexer_1_out13), .out14(demultiplexer_1_out14),
    .out15(demultiplexer_1_out15), .out16(demultiplexer_1_out16), .in(Enable), .sel(Addr[4:0]));  // open: out17, out18, out19, out20, out21, out22, out23, out24, out25, out26, out27, out28, out29, out30, out31
  Register #(.width(16)) register_1 (.D(Data), .en(demultiplexer_1_out0), .Q(register_1_q), .clk(Takt));  // open: clr
  Register #(.width(16)) register_2 (.D(Data), .en(demultiplexer_1_out1), .Q(register_2_q), .clk(Takt));  // open: clr
  Register #(.width(16)) register_3 (.D(Data), .en(demultiplexer_1_out2), .Q(register_3_q), .clk(Takt));  // open: clr
  Register #(.width(16)) register_4 (.D(Data), .en(demultiplexer_1_out3), .Q(register_4_q), .clk(Takt));  // open: clr
  Register #(.width(16)) register_5 (.D(Data), .en(demultiplexer_1_out4), .Q(register_5_q), .clk(Takt));  // open: clr
  Register #(.width(16)) register_6 (.D(Data), .en(demultiplexer_1_out5), .Q(register_6_q), .clk(Takt));  // open: clr
  Register #(.width(16)) register_7 (.D(Data), .en(demultiplexer_1_out6), .Q(register_7_q), .clk(Takt));  // open: clr
  Register #(.width(16)) register_8 (.D(Data), .en(demultiplexer_1_out7), .Q(register_8_q), .clk(Takt));  // open: clr
  Register #(.width(16)) register_9 (.D(Data), .en(demultiplexer_1_out8), .Q(register_9_q), .clk(Takt));  // open: clr
  Register #(.width(16)) register_10 (.D(Data), .en(demultiplexer_1_out9), .Q(register_10_q), .clk(Takt));  // open: clr
  Register #(.width(16)) register_11 (
    .D(Data), .en(demultiplexer_1_out10), .Q(register_11_q), .clk(Takt));  // open: clr
  Register #(.width(16)) register_12 (
    .D(Data), .en(demultiplexer_1_out11), .Q(register_12_q), .clk(Takt));  // open: clr
  Register #(.width(16)) register_13 (
    .D(Data), .en(demultiplexer_1_out12), .Q(register_13_q), .clk(Takt));  // open: clr
  Register #(.width(16)) register_14 (
    .D(Data), .en(demultiplexer_1_out13), .Q(register_14_q), .clk(Takt));  // open: clr
  Register #(.width(16)) register_15 (
    .D(Data), .en(demultiplexer_1_out14), .Q(register_15_q), .clk(Takt));  // open: clr
  Register #(.width(16)) register_16 (
    .D(Data), .en(demultiplexer_1_out15), .Q(register_16_q), .clk(Takt));  // open: clr
  Register #(.width(16)) register_17 (
    .D(register_1_q), .en(demultiplexer_1_out16), .Q(out_5), .clk(Takt));  // open: clr
  Register #(.width(16)) register_18 (
    .D(register_2_q), .en(demultiplexer_1_out16), .Q(out_6), .clk(Takt));  // open: clr
  Register #(.width(16)) register_19 (
    .D(register_3_q), .en(demultiplexer_1_out16), .Q(out_7), .clk(Takt));  // open: clr
  Register #(.width(16)) register_20 (
    .D(register_4_q), .en(demultiplexer_1_out16), .Q(out_8), .clk(Takt));  // open: clr
  Register #(.width(16)) register_21 (
    .D(register_5_q), .en(demultiplexer_1_out16), .Q(out_9), .clk(Takt));  // open: clr
  Register #(.width(16)) register_22 (
    .D(register_6_q), .en(demultiplexer_1_out16), .Q(out_10), .clk(Takt));  // open: clr
  Register #(.width(16)) register_23 (
    .D(register_7_q), .en(demultiplexer_1_out16), .Q(out_11), .clk(Takt));  // open: clr
  Register #(.width(16)) register_24 (
    .D(register_8_q), .en(demultiplexer_1_out16), .Q(out_12), .clk(Takt));  // open: clr
  Register #(.width(16)) register_25 (
    .D(register_9_q), .en(demultiplexer_1_out16), .Q(out_13), .clk(Takt));  // open: clr
  Register #(.width(16)) register_26 (
    .D(register_10_q), .en(demultiplexer_1_out16), .Q(out_14), .clk(Takt));  // open: clr
  Register #(.width(16)) register_27 (
    .D(register_11_q), .en(demultiplexer_1_out16), .Q(out_15), .clk(Takt));  // open: clr
  Register #(.width(16)) register_28 (
    .D(register_12_q), .en(demultiplexer_1_out16), .Q(out_16), .clk(Takt));  // open: clr
  Register #(.width(16)) register_29 (
    .D(register_13_q), .en(demultiplexer_1_out16), .Q(out_17), .clk(Takt));  // open: clr
  Register #(.width(16)) register_30 (
    .D(register_14_q), .en(demultiplexer_1_out16), .Q(out_18), .clk(Takt));  // open: clr
  Register #(.width(16)) register_31 (
    .D(register_15_q), .en(demultiplexer_1_out16), .Q(out_19), .clk(Takt));  // open: clr
  Register #(.width(16)) register_32 (
    .D(register_16_q), .en(demultiplexer_1_out16), .Q(out_20), .clk(Takt));  // open: clr
endmodule

module terminal (
  input  [15:0] data,
  input  [15:0] addr,
  input  io_Write,
  output [6:0] ASCII,
  output TermEnable
);

  wire comparator_1_eq;

  Comparator #(.width(16)) comparator_1 (.a(addr), .b(16'h1f), .eq(comparator_1_eq));  // open: gt, lt
  and and_1 (TermEnable, comparator_1_eq, io_Write);

  assign ASCII = data[6:0];
endmodule

module GPO (
  input  [15:0] data,
  input  [15:0] addr,
  input  io_Write,
  input  clock,
  output out_5,
  output out_6,
  output out_7,
  output out_8,
  output out_9,
  output out_10,
  output out_11,
  output out_12,
  output out_13,
  output out_14,
  output out_15,
  output out_16,
  output out_17,
  output out_18,
  output out_19,
  output out_20
);

  wire and_1_out, comparator_1_eq;

  Comparator #(.width(16)) comparator_1 (.a(addr), .b(16'h15), .eq(comparator_1_eq));  // open: gt, lt
  and and_1 (and_1_out, comparator_1_eq, io_Write);
  Register #(.width(16)) register_1 (
    .D(data), .en(and_1_out),
    .Q({out_20, out_19, out_18, out_17, out_16, out_15, out_14, out_13, out_12, out_11, out_10, out_9, out_8, out_7, out_6, out_5}),
    .clk(clock));  // open: clr
endmodule

module GPI (
  input  in_1,
  input  in_2,
  input  in_3,
  input  in_4,
  input  in_5,
  input  in_6,
  input  in_7,
  input  in_8,
  input  in_9,
  input  in_10,
  input  in_11,
  input  in_12,
  input  in_13,
  input  [15:0] addr,
  input  in_15,
  input  in_16,
  input  in_17,
  input  io_Read,
  output [15:0] data
);

  wire and_1_out, comparator_1_eq;

  Comparator #(.width(16)) comparator_1 (.a(addr), .b(16'h14), .eq(comparator_1_eq));  // open: gt, lt
  and and_1 (and_1_out, comparator_1_eq, io_Read);
  assign data = and_1_out ? {in_17, in_16, in_15, in_13, in_12, in_11, in_10, in_9, in_8, in_7, in_6, in_5, in_4, in_3, in_2, in_1} : 16'bz;  // Controlled_Buffer controlled_buffer_1

  // Notes on the sheet:
  //   in_17: pull=down
  //   in_8: pull=down
  //   in_16: pull=down
  //   in_4: pull=down
  //   in_3: pull=down
  //   in_7: pull=down
  //   in_6: pull=down
  //   in_10: pull=down
  //   in_12: pull=down
  //   in_2: pull=down
  //   in_11: pull=down
  //   in_15: pull=down
  //   in_1: pull=down
  //   in_5: pull=down
  //   in_9: pull=down
  //   in_13: pull=down
endmodule

module keyboard (
  input  [6:0] ASCII,
  input  [15:0] addr,
  input  io_Read,
  output [15:0] data,
  output Enable
);

  wire comparator_1_eq;

  Comparator #(.width(16)) comparator_1 (.a(addr), .b(16'h16), .eq(comparator_1_eq));  // open: gt, lt
  and and_1 (Enable, comparator_1_eq, io_Read);
  assign data = Enable ? {{9{1'b0}}, ASCII} : 16'bz;  // Controlled_Buffer controlled_buffer_1
endmodule
