// Digital circuit ProcessorTestTemplate.dig as structural Verilog
module ProcessorTestTemplate (
  input  Clk
);

  wire processor_1_p2, processor_1_p3, processor_1_p4, processor_1_p5;

  // Processor processor_1: pin names not known; wires that end beside it: Clk, processor_1_p2, processor_1_p3, processor_1_p4, processor_1_p5
  // TestOut #(.generic("addr := 3;")) Reg3: pin names not known; wires that end beside it: processor_1_p2, processor_1_p3, processor_1_p4, processor_1_p5, Clk
  // TestOut #(.generic("addr := 32;")) Reg32: pin names not known; wires that end beside it: processor_1_p2, processor_1_p3, processor_1_p4, processor_1_p5, Clk

  // Notes on the sheet:
  //   Clk: Hz: 2147483647
endmodule
